# Fritzing sketch incubatrice_1 (saved by Fritzing 0.9.5d)

parts:
  LED4 = LED - 3mm [color="Green (555nm)" package="3 mm [THT]"]
  U1 = SWITCH_SPDT [package=kps-1290]
  U2 = SWITCH_SPDT [package=kps-1290]
  U3 = SWITCH_SPDT [package=kps-1290]
  R2 = Rotary Potentiometer (Small) [maximum_resistance=10kΩ package=THT]
  R1 = Rotary Potentiometer (Small) [maximum_resistance=10kΩ package=THT]
  LED5 = LED - 3mm [color="Red (633nm)" package="3 mm [THT]"]
  LED2 = LED - 3mm [color="Red (633nm)" package="3 mm [THT]"]
  J7 = Camdenboss CTB0158-2 [part_number=CTB0158-2 package=THT]
  J15 = Camdenboss CTB0158-2 [part_number=CTB0158-2 package=THT]
  LED3 = LED - 3mm [color="Green (555nm)" package="3 mm [THT]"]
  Part9 = LCD2004-I2C
  Part10 = JST-XH-4A-F [package=THT]
  Part11 = JST-XH-4A-F [package=THT]
  Part12 = JST-XH-4A-F [package=THT]
  Part13 = JST-XH-4A-M [package=THT]  # not connected
  Part14 = JST-XH-4A-M [package=THT]  # not connected
  Part15 = JST-XH-4A-M [package=THT]  # not connected
  Part16 = JST-XH-2A-F [package=THT]
  Part17 = JST-XH-2A-M [package=THT]  # not connected
  SHT3x1 = SHT3x  # not connected

nets:
  N1: LED4.cathode, U1.O, U2.O, U3.O, R2.leg1, R1.leg1, LED5.cathode, LED2.cathode, J7.pin2, J7.terminal_2, J15.pin1, LED3.cathode, Part9.GND
  N2: LED4.anode, Part10.pin2
  N3: U1.P, Part11.pin2
  N4: U1.S, U2.S, U3.S, R2.leg2, R1.leg2, J7.pin1, J7.terminal_1, J15.pin2, Part9.VCC
  N5: U2.P, Part11.pin3
  N6: U3.P, Part11.pin4
  N7: R2.wiper, Part12.pin3
  N8: R1.wiper, Part12.pin4
  N9: LED5.anode, Part10.pin1
  N10: LED2.anode, Part10.pin4
  N11: J15.terminal_1, Part16.pin2
  N12: J15.terminal_2, Part16.pin1
  N13: LED3.anode, Part10.pin3
  N14: Part9.SDA, Part12.pin2
  N15: Part9.SCL, Part12.pin1

notes:
  REFILL
  RH ON
  HEAT ON
  ALARM
  LIGHT
  HUMIDIFIER
  HEATER
  RH
  TEMP
  VCC
  GND
  RH POTENTIOMETER
  TEMP POTENTIOMETER
  LIGHT SWITCH
  HUMIDIFIER SWITCH
  HEATER SWITCH
  REFILL LED
  RH ON LED
  HEAT ON LED
  ALARM LED
  SDA
  SCL
  NC
  (to the arduino board)
  I2C DISPLAY

custom parts:
  LCD2004-I2C: A standard character display with 4x20 characters. Comes in many colors with LCM2004 IIC attached.
  JST-XH-4A-F: 4 pin female JST XH connector
  JST-XH-4A-M: 4 pin male JST XH connector
  JST-XH-2A-F: 2 pin female JST XH connector
  JST-XH-2A-M: 2 pin make JST XH connector
  SHT3x: SHT31 SHT35
