# Fritzing sketch incubatrice_2 (saved by Fritzing 0.9.5d)
breadboards: 1

parts:
  R1 = Resistor [tolerance=±5% resistance=220 package=THT]
  R2 = Resistor [tolerance=±5% resistance=470 package=THT]
  Part2 = Arduino Mega 2560 (Rev3)
  R3 = Resistor [tolerance=±5% resistance=220 package=THT]
  R4 = Resistor [tolerance=±5% resistance=470 package=THT]
  J10 = Camdenboss CTB0158-11 [part_number=CTB0158-11 package=THT]
  J8 = Camdenboss CTB0158-11 [part_number=CTB0158-11 package=THT]
  J9 = Camdenboss CTB0158-4 [part_number=CTB0158-4 package=THT]
  J12 = Camdenboss CTB0158-4 [part_number=CTB0158-4 package=THT]
  J13 = Camdenboss CTB0158-2 [part_number=CTB0158-2 package=THT]
  J14 = Camdenboss CTB0158-2 [part_number=CTB0158-2 package=THT]

nets:
  N1: R1.Pin_0, Part2.D3_PWM
  N2: R1.Pin_1, J8.terminal_6
  N3: R2.Pin_0, Part2.D2_PWM
  N4: R2.Pin_1, J8.terminal_5
  N5: Part2.A0, J8.terminal_2
  N6: Part2.A1, J8.terminal_1
  N7: Part2.D21/SCL, J8.terminal_3
  N8: Part2.D20/SDA, J8.terminal_4
  N9: Part2.D12_PWM, J9.terminal_4
  N10: Part2.D11_PWM, J9.terminal_3
  N11: Part2.D10_PWM, J9.terminal_2
  N12: Part2.D9_PWM, J9.terminal_1
  N13: Part2.D8_PWM, J8.terminal_11
  N14: Part2.5V, J14.terminal_1
  N15: Part2.GND, J14.terminal_2
  N16: Part2.D4_PWM, R3.Pin_0
  N17: Part2.D5_PWM, R4.Pin_0
  N18: Part2.D6_PWM, J8.terminal_9
  N19: Part2.D7_PWM, J8.terminal_10
  N20: R3.Pin_1, J8.terminal_7
  N21: R4.Pin_1, J8.terminal_8
  N22: J10.pin1, J10.terminal_1, J8.pin11
  N23: J10.pin2, J10.terminal_2, J8.pin10
  N24: J10.pin3, J10.terminal_3, J8.pin9
  N25: J10.pin4, J10.terminal_4, J8.pin8
  N26: J10.pin5, J10.terminal_5, J8.pin7
  N27: J10.pin6, J10.terminal_6, J8.pin6
  N28: J10.pin7, J10.terminal_7, J8.pin5
  N29: J10.pin8, J10.terminal_8, J8.pin4
  N30: J10.pin9, J10.terminal_9, J8.pin3
  N31: J10.pin10, J10.terminal_10, J8.pin2
  N32: J10.pin11, J10.terminal_11, J8.pin1
  N33: J9.pin1, J12.pin4, J12.terminal_4
  N34: J9.pin2, J12.pin3, J12.terminal_3
  N35: J9.pin3, J12.pin2, J12.terminal_2
  N36: J9.pin4, J12.pin1, J12.terminal_1
  N37: J13.pin1, J14.pin2
  N38: J13.pin2, J14.pin1

notes:
  SCL
  SDA
  ALARM LED
  HEAT ON LED
  RH ON LED
  REFILL LED
  HEATER SWITCH
  HUMIDIFIER SWITCH
  LIGHT SWITCH
  TEMP POTENTIOMETER
  RH POTENTIOMETER
  GND
  VCC
  AUX FAN RELAY
  LIGHT RELAY
  HUMIDIFIER RELAY
  HEATER RELAY
  (to the front panel and SHT20)
  (to the relay board and step down)
  (front panel and SHT20)
  (to the front panel)
  (front panel)
  (to the relay board)
